// Logisim project banco de registradores.circ as structural Verilog: 2 circuits, main circuit main
module main (
  input  [7:0] in_1,
  input  in_2,
  output [7:0] out_3
);

  D_Flip_Flop d_ff_1 (.clk(in_2), .D(in_1[0]), .Q(out_3[0]));  // open: Qn, preset, en, reset
  D_Flip_Flop d_ff_2 (.clk(in_2), .D(in_1[1]), .Q(out_3[1]));  // open: Qn, preset, en, reset
  D_Flip_Flop d_ff_3 (.clk(in_2), .D(in_1[2]), .Q(out_3[2]));  // open: Qn, preset, en, reset
  D_Flip_Flop d_ff_4 (.clk(in_2), .D(in_1[3]), .Q(out_3[3]));  // open: Qn, preset, en, reset
  D_Flip_Flop d_ff_5 (.clk(in_2), .D(in_1[4]), .Q(out_3[4]));  // open: Qn, preset, en, reset
  D_Flip_Flop d_ff_6 (.clk(in_2), .D(in_1[5]), .Q(out_3[5]));  // open: Qn, preset, en, reset
  D_Flip_Flop d_ff_7 (.clk(in_2), .D(in_1[6]), .Q(out_3[6]));  // open: Qn, preset, en, reset
  D_Flip_Flop d_ff_8 (.clk(in_2), .D(in_1[7]), .Q(out_3[7]));  // open: Qn, preset, en, reset
endmodule

module banco (
  input  [7:0] in_1,
  input  [3:0] in_2,
  input  [7:0] in_3,
  input  [3:0] seletor_da_saida
);

  wire clock_1_out, demultiplexer_1_out0, demultiplexer_1_out1, demultiplexer_1_out2, demultiplexer_1_out3,
       demultiplexer_1_out4, demultiplexer_1_out5, demultiplexer_1_out6, demultiplexer_1_out7,
       demultiplexer_1_out8, demultiplexer_1_out9, demultiplexer_1_out10, demultiplexer_1_out11,
       demultiplexer_1_out12, demultiplexer_1_out13, demultiplexer_1_out14, demultiplexer_1_out15;
  wire [7:0] main_1_out_3, main_2_out_3, main_3_out_3, main_4_out_3, main_5_out_3, main_6_out_3,
       main_7_out_3, main_8_out_3, main_9_out_3, main_10_out_3, main_11_out_3, main_12_out_3, main_13_out_3,
       main_14_out_3, main_15_out_3, main_16_out_3;

  Demultiplexer #(.select(4)) demultiplexer_1 (
    .out0(demultiplexer_1_out0), .out1(demultiplexer_1_out1), .out2(demultiplexer_1_out2),
    .out3(demultiplexer_1_out3), .out4(demultiplexer_1_out4), .out5(demultiplexer_1_out5),
    .out6(demultiplexer_1_out6), .out7(demultiplexer_1_out7), .out8(demultiplexer_1_out8),
    .out9(demultiplexer_1_out9), .out10(demultiplexer_1_out10), .out11(demultiplexer_1_out11),
    .out12(demultiplexer_1_out12), .out13(demultiplexer_1_out13), .out14(demultiplexer_1_out14),
    .out15(demultiplexer_1_out15), .in(clock_1_out), .sel(in_2));  // open: en
  Clock clock_1 (.out(clock_1_out));
  main main_1 (.in_1(in_1), .in_2(demultiplexer_1_out0), .out_3(main_1_out_3));
  main main_2 (.in_1(in_1), .in_2(demultiplexer_1_out1), .out_3(main_2_out_3));
  main main_3 (.in_1(in_1), .in_2(demultiplexer_1_out2), .out_3(main_3_out_3));
  main main_4 (.in_1(in_1), .in_2(demultiplexer_1_out3), .out_3(main_4_out_3));
  main main_5 (.in_1(in_1), .in_2(demultiplexer_1_out4), .out_3(main_5_out_3));
  main main_6 (.in_1(in_1), .in_2(demultiplexer_1_out5), .out_3(main_6_out_3));
  main main_7 (.in_1(in_1), .in_2(demultiplexer_1_out6), .out_3(main_7_out_3));
  main main_8 (.in_1(in_1), .in_2(demultiplexer_1_out7), .out_3(main_8_out_3));
  main main_9 (.in_1(in_1), .in_2(demultiplexer_1_out8), .out_3(main_9_out_3));
  Multiplexer #(.select(4), .width(8)) multiplexer_1 (
    .in0(main_1_out_3), .in1(main_2_out_3), .in2(main_3_out_3), .in3(main_4_out_3), .in4(main_5_out_3),
    .in5(main_6_out_3), .in6(main_7_out_3), .in7(main_8_out_3), .in8(main_9_out_3), .in9(main_10_out_3),
    .in10(main_11_out_3), .in11(main_12_out_3), .in12(main_13_out_3), .in13(main_14_out_3),
    .in14(main_15_out_3), .in15(main_16_out_3), .out(in_3), .sel(seletor_da_saida));  // open: en
  main main_10 (.in_1(in_1), .in_2(demultiplexer_1_out9), .out_3(main_10_out_3));
  main main_11 (.in_1(in_1), .in_2(demultiplexer_1_out10), .out_3(main_11_out_3));
  main main_12 (.in_1(in_1), .in_2(demultiplexer_1_out11), .out_3(main_12_out_3));
  main main_13 (.in_1(in_1), .in_2(demultiplexer_1_out12), .out_3(main_13_out_3));
  main main_14 (.in_1(in_1), .in_2(demultiplexer_1_out13), .out_3(main_14_out_3));
  main main_15 (.in_1(in_1), .in_2(demultiplexer_1_out14), .out_3(main_15_out_3));
  main main_16 (.in_1(in_1), .in_2(demultiplexer_1_out15), .out_3(main_16_out_3));

  // Notes on the sheet:
  //   clock
  //   seletor da entrada
  //   entrada
  //   saida
endmodule
